# Fritzing sketch Ironman_moodlight_circuit (saved by Fritzing 0.9.3b)
breadboards: 1

parts:
  LCD1 = LCD screen
  C1 = Electrolytic Capacitor [capacitance=1µF package="100 mil [THT, electrolytic]"]
  R1 = Resistor [tolerance=±5% resistance=150 package=THT]
  R2 = Rotary Potentiometer (Small) [maximum_resistance=100kΩ package=THT]
  U1 = Sharp Dust Sensor [part_number=GP2Y1010AU0F]
  부품2 = Adafruit APDS-9960 [part_number="Adafruit #3595"]  # not connected
  부품3 = Arduino Uno (Rev3) - ICSP  # not connected
  부품1 = 24 NeoPixel Ring [part_number=1586]
  BT1 = Bluetooth HC-06d [package=THT]
  부품4 = Adafruit Proto Shield R3 [part_number="Adafruit #2077"]
  LCM1602_IIC1 = LCM1602 IIC [part_number="LCM1602 IIC" chip_label="LCM1602 IIC" package="DIP (Dual Inline) [THT]"]

nets:
  N1: LCD1.VSS, LCM1602_IIC1.K
  N2: LCD1.VDD, LCM1602_IIC1.A
  N3: LCD1.V0, LCM1602_IIC1.D7
  N4: LCD1.RS, LCM1602_IIC1.D6
  N5: LCD1.R/W, LCM1602_IIC1.D5
  N6: LCD1.E, LCM1602_IIC1.D4
  N7: LCD1.DB0, LCM1602_IIC1.D3
  N8: LCD1.DB1, LCM1602_IIC1.D2
  N9: LCD1.DB2, LCM1602_IIC1.D1
  N10: LCD1.DB3, LCM1602_IIC1.D0
  N11: LCD1.DB4, LCM1602_IIC1.E
  N12: LCD1.DB5, LCM1602_IIC1.RW
  N13: LCD1.DB6, LCM1602_IIC1.RS
  N14: LCD1.DB7, LCM1602_IIC1.V0
  N15: LCD1.LED+, LCM1602_IIC1.VDD
  N16: LCD1.LED-, LCM1602_IIC1.VSS
  GND: C1.-, R1.Pin_1, R2.leg1, U1.LED, U1.Vo, BT1.GND, 부품4.GND, LCM1602_IIC1.SCL
  N17: C1.+, R1.Pin_0, U1.VCC
  N18: R2.wiper, 부품4.A1, LCM1602_IIC1.SDA
  VCC: U1.V-LED, BT1.VCC, 부품4.+5V
  N19: U1.LED-GND, 부품4.A2
  N20: U1.S-GND, 부품4.D8
  N21: 부품1.5V, 부품1.D0
  N22: BT1.TXD, 부품4.D6
  N23: BT1.RXD, 부품4.D7
  N24: 부품4.A4, LCM1602_IIC1.VCC
  N25: 부품4.A5, LCM1602_IIC1.GND

custom parts:
  Sharp Dust Sensor: Sharp GP2Y1010AU0F Dust Sensor
  Adafruit APDS-9960: The APDS9960 from Avago Technologies has an integrated IR LED and driver, along with four directional photodiodes that sense reflected IR energy from the LED. It's proximity detection feature allows it to measure the distance an object is from the front of the sensor (up to a few centimeters) with 8 bit resolution. Since there are four IR sensors, you can measure the changes in light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
  24 NeoPixel Ring: 24 ultra bright smart LED NeoPixels are arranged in a circle with 2.6" (66mm) outer diameter. The rings are 'chainable' - connect the output pin of one to the input pin of another. Use only one microcontroller pin to control as many as you can chain together! Each LED is addressable as the driver chip is inside the LED. Each one has ~18mA constant current drive so the color will be very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
  Bluetooth HC-06d: Bluetooth HC-06 - face down, pins down 16.5mm x 37.5mm PCB
  Adafruit Proto Shield R3: This prototyping shield is the best out there (well, we think so, at least), and now is even better with Version R3 - updated for the most compatibility with just about all the Arduinos! It works with UNO, Mega, Leonardo, NG, Diecimila, Duemilanove, and compatible Arduinos. Yun's and Arduino Ethernets have a chunky Ethernet jack that gets in the way of stacking, you can use the stacking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
  LCM1602 IIC: I2C-Module to use a 1602 or 2004 LCD on with the wire.h libory Serial LCD Modul
